# Fritzing sketch watering-timer (saved by Fritzing 0.9.2b)
breadboards: 1

parts:
  U1 = ESP8266-12e_tht [part_number=ESP8266-12E]
  S1 = SPST Switch [package=switch-spdt_kit]
  R1 = Resistor [tolerance=±5% resistance=10k package=THT]
  U2 = Voltage Regulator - 3.3V [part_number=LM317 package="TO220 [THT]"]
  R2 = Resistor [tolerance=±5% resistance=220 package=THT]
  C1 = Tantalum Capacitor [capacitance=10µF package="100 mil [THT, tantalum]"]
  D1 = Rectifier Diode [part_number=1N4007 package="300 mil [THT]"]
  S4 = Pushbutton [package=THT]
  JBAT = Screw terminal - 2 pins [package=THT]
  R3 = Resistor [tolerance=±5% resistance=390 package=THT]
  R4 = Resistor [tolerance=±5% resistance=10k package=THT]
  R5 = Resistor [tolerance=±5% resistance=10k package=THT]
  R6 = Resistor [tolerance=±5% resistance=10k package=THT]
  R7 = Resistor [tolerance=±5% resistance=10k package=THT]

nets:
  RESET: U1.REST, U1.GPIO_16, R1.Pin_1, S4.leg1
  3.3V: U1.VCC, R1.Pin_0, U2.output_voltage, R2.Pin_0, D1.cathode, R4.Pin_0, R5.Pin_0
  GND: U1.GND, C1.-, S4.leg0, JBAT.pin2, R3.Pin_1, R6.Pin_1, R7.Pin_1
  GPIO15: U1.GPIO_15, R6.Pin_0
  GPIO2: U1.GPIO_2, R5.Pin_1
  GPIO0: U1.GPIO_0, S1.P
  N1: S1.O, R4.Pin_1
  N2: S1.S, R7.Pin_0
  VBAT: U2.input_voltage, JBAT.pin1
  N3: U2.GND, R2.Pin_1, C1.+, D1.anode, R3.Pin_0

notes:
  flash mode
  Reset Button
  3.3v DC power

custom parts:
  ESP8266-12e_tht: These are the first series of modules made with the ESP8266 by the third-party manufacturer AI-Thinker and remain the most widely available. They are collectively referred to as "ESP-xx modules" and to form a workable development system require additional components, especially a serial TTL-to-USB adapter (sometimes called a USB-to-UART bridge) and an external 3.3V power supply. The pcb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
